# Fritzing sketch servo (saved by Fritzing 0.9.3b)
breadboards: 1

parts:
  Part1 = Arduino Uno (Rev3)
  Part2 = Servo Improved
  BAT6 = Battery Holders [package=battery-aa-kit]
  BAT7 = Battery Holders [package=battery-aa-kit]
  BAT8 = Battery Holders [package=battery-aa-kit]
  BAT9 = Battery Holders [package=battery-aa-kit]

nets:
  N1: Part1.D5_PWM, Part2.signal
  N2: Part1.GND, Part2.ground, BAT9.+
  N3: Part2.vcc, BAT6.-
  N4: BAT6.+, BAT8.-
  N5: BAT7.+, BAT9.-
